# Fritzing sketch protoboardDessign (saved by Fritzing 0.9.3b)
breadboards: 1

parts:
  Componente1 = Arduino Uno (Rev3)
  R1 = Resistor [tolerance=±5% resistance=220 package=THT]
  R2 = Resistor [tolerance=±5% resistance=220 package=THT]
  R3 = Resistor [tolerance=±5% resistance=220 package=THT]  # not connected
  LED1 = LED - 5mm [color="Red (633nm)" package="5 mm [THT]"]
  LED2 = LED - 5mm [color="Yellow (592nm)" package="5 mm [THT]"]
  LED3 = LED - 5mm [color="Green (560nm)" package="5 mm [THT]"]

nets:
  N1: Componente1.D8, R2.Pin_0
  N2: Componente1.GND, LED1.anode, LED2.anode, LED3.anode
  N3: Componente1.D7, R1.Pin_0
  N4: R1.Pin_1, LED3.cathode
  N5: R2.Pin_1, LED2.cathode

notes:
  Las resistencias son de 220 ohms
