# Fritzing sketch protoboardDessign (saved by Fritzing 0.9.3b)
breadboards: 1

parts:
  Componente1 = Arduino Uno (Rev3)
  R1 = Resistor [tolerance=±5% resistance=1k package=THT]
  Q1 = NPN-Transistor [package="TO92 [THT]"]
  J1 = Piezo Speaker
  R2 = Resistor [tolerance=±5% resistance=220 package=THT]
  LED1 = LED - 5mm [color="Yellow (592nm)" package="5 mm [THT]"]  # not connected
  LED2 = LED - 5mm [color="Green (565nm)" package="5 mm [THT]"]

nets:
  N1: Componente1.D8, R1.Pin_0
  N2: Componente1.5V, J1.pin2, R2.Pin_1
  N3: Componente1.GND, Q1.E, LED2.anode
  N4: R1.Pin_1, Q1.B
  N5: Q1.C, J1.pin1
